# Fritzing sketch 4 (saved by Fritzing 0.9.4)
breadboards: 1

parts:
  U1 = NodeMCU V1.0
  LED1 = LED - 5mm [color="Red (633nm)" package="5 mm [THT]"]
  U2 = POT [package=pot_mammoth]
  R1 = Resistor [tolerance=±5% resistance=220 package=THT]

nets:
  N1: U1.D5, LED1.cathode
  N2: U1.GND#13, U2.E, R1.Pin_1
  N3: U1.3V3#14, U2.S
  N4: U1.A0, U2.A
  N5: LED1.anode, R1.Pin_0

custom parts:
  NodeMCU V1.0: ESP8266 based NodeMCU V1.0
