# Fritzing sketch 6 (saved by Fritzing 0.9.4)
breadboards: 1

parts:
  U1 = NodeMCU V1.0
  R1 = Resistor [tolerance=±5% resistance=220 package=THT]
  LED1 = LED - 5mm [color="Red (633nm)" package="5 mm [THT]"]
  hc-sr1 = hc-sr04
  IC1 = Voltage Regulator [package=to-220-alt]
  VCC1 = Battery block 9V

nets:
  N1: U1.D1, hc-sr1.Echo
  N2: U1.D2, hc-sr1.Trig
  N3: U1.GND#6, R1.Pin_0
  N4: U1.D5, LED1.anode
  N5: R1.Pin_1, LED1.cathode
  N6: hc-sr1.VCC, IC1.OUT
  N7: hc-sr1.GND, IC1.IN, VCC1.-
  N8: IC1.GND, VCC1.+

custom parts:
  NodeMCU V1.0: ESP8266 based NodeMCU V1.0
